// Logisim project timer_.circ as structural Verilog
module Timer (
  input  [3:0] Boutons,
  input  [2:0] Etat,
  input  [22:0] Temps
);

  wire comparator_1_eq;

  Comparator #(.width(3)) comparator_1 (.a(Etat), .b(3'b011), .eq(comparator_1_eq));  // open: gt, lt
endmodule
